# Fritzing sketch printer (saved by Fritzing 0.7.5b)
breadboards: 1

parts:
  S1 = Pushbutton [package="[THT]"]
  LED2 = LED - 5mm [color="Green (555nm)" package="5 mm [THT]"]
  LED3 = LED - 5mm [color="Yellow (595nm)" package="5 mm [THT]"]
  LED4 = LED - 5mm [color="Red (633nm)" package="5 mm [THT]"]
  R2 = Resistor [tolerance=±5% resistance=220 package=THT]
  R5 = Resistor [tolerance=±5% resistance=220 package=THT]
  R6 = Resistor [tolerance=±5% resistance=220 package=THT]
  R7 = Resistor [tolerance=±5% resistance=220 package=THT]
  J1 = male pin header, 2 pins [form="♂ (male)"]
  J2 = male pin header, 3 pins [form="♂ (male)"]
  Arduino_Ethernet_Shield1 = Arduino Ethernet Shield
  Part1 = Thermal Printer

nets:
  N1: S1.Pin_1, S1.Pin_2, R7.Pin_0, Arduino_Ethernet_Shield1.D3
  N2: S1.Pin_3, S1.Pin_4
  N3: LED2.cathode, R2.Pin_0
  N4: LED2.anode, Arduino_Ethernet_Shield1.D5
  N5: LED3.cathode, R5.Pin_0
  N6: LED3.anode, Arduino_Ethernet_Shield1.D6
  N7: LED4.cathode, R6.Pin_0
  N8: LED4.anode, Arduino_Ethernet_Shield1.D7
  N9: R2.Pin_1, R5.Pin_1, R7.Pin_1
  GND: R6.Pin_1, J1.pin2, J2.pin3, Arduino_Ethernet_Shield1.GND, Part1.GND
  N10: J1.pin1, Arduino_Ethernet_Shield1.VIN, Part1.VH
  N11: J2.pin1, Arduino_Ethernet_Shield1.D8, Part1.TXD
  N12: J2.pin2, Arduino_Ethernet_Shield1.D9, Part1.RXD
